// Logisim project 2 BIT-ALU.circ as structural Verilog: 1 circuit, main circuit main
module main (
  input  [1:0] A,
  input  [1:0] B,
  input  [1:0] in_3,
  input  [1:0] in_4,
  input  S2,
  input  S1,
  input  S0,
  input  in_8,
  input  in_9,
  output [1:0] out_10,
  output [1:0] out_11
);

  wire [1:0] adder_1_out, and_1_out, multiplexer_1_out, multiplexer_2_out, not_1_out, not_2_out, or_1_out,
       xor_1_out;

  assign not_1_out = ~B;  // NOT_Gate not_1, 2 bits wide
  assign and_1_out = A & B;  // AND_Gate and_1, 2 bits wide
  assign or_1_out = A | B;  // OR_Gate or_1, 2 bits wide
  assign xor_1_out = A ^ B;  // XOR_Gate xor_1, 2 bits wide
  Multiplexer #(.select(2), .width(2)) multiplexer_1 (
    .in0(B), .in1(in_3), .in2(in_4), .in3(not_1_out), .out(multiplexer_1_out), .sel({S2, S1}));
  assign not_2_out = ~A;  // NOT_Gate not_2, 2 bits wide
  Adder #(.width(2)) adder_1 (.a(A), .b(multiplexer_1_out), .out(adder_1_out), .cin(S1));  // open: cout
  Multiplexer #(.select(2), .width(2)) multiplexer_2 (
    .in0(and_1_out), .in1(or_1_out), .in2(not_2_out), .in3(xor_1_out), .out(multiplexer_2_out),
    .sel({in_8, in_9}));
  Multiplexer #(.width(2)) multiplexer_3 (.in0(adder_1_out), .in1(multiplexer_2_out), .out(out_10), .sel(S0));
endmodule
